// Logisim project lab3.circ as structural Verilog: 1 circuit, main circuit main
module main (
  input  in_1,
  input  in_2,
  output out_3,
  output out_4
);

  xor xor_1 (out_3, ~in_1, in_2);  // XOR_Gate
  and and_1 (out_4, out_3, in_2);
endmodule
